// Logisim project hw_vga_sim.circ as structural Verilog: 1 circuit, main circuit main
module main (
  input  nRST
);

  wire clock_1_out, n74163_1_pin3, n74163_1_pin7, n74163_1_pin15, n74163_2_pin15;
  wire [3:0] n74163_1_pin14, n74163_2_pin14, n74163_3_pin15;

  Clock clock_1 (.out(clock_1_out));
  _7411 #(.ShowInternalStructure("true")) u_7411_1 ();  // open: pin1, pin2, pin3, pin4, pin5, pin6, pin13, pin12, pin11, pin10, pin9, pin8
  _74163 #(.ShowInternalStructure("true")) u_74163_1 (
    .pin1(nRST), .pin2(clock_1_out), .pin3(n74163_1_pin3), .pin4(n74163_1_pin3), .pin5(n74163_1_pin3),
    .pin6(n74163_1_pin3), .pin7(n74163_1_pin7), .pin15(n74163_1_pin15), .pin14(n74163_1_pin14[0]),
    .pin13(n74163_1_pin14[1]), .pin12(n74163_1_pin14[2]), .pin11(n74163_1_pin14[3]), .pin10(n74163_1_pin7),
    .pin9(n74163_1_pin7));
  _74163 #(.ShowInternalStructure("true")) u_74163_2 (
    .pin1(nRST), .pin2(clock_1_out), .pin3(n74163_1_pin3), .pin4(n74163_1_pin3), .pin5(n74163_1_pin3),
    .pin6(n74163_1_pin3), .pin7(n74163_1_pin15), .pin15(n74163_2_pin15), .pin14(n74163_2_pin14[0]),
    .pin13(n74163_2_pin14[1]), .pin12(n74163_2_pin14[2]), .pin11(n74163_2_pin14[3]), .pin10(n74163_1_pin15),
    .pin9(n74163_1_pin7));
  Hex_Digit_Display hex_digit_display_1 (.value(n74163_1_pin14));  // open: dp
  Hex_Digit_Display hex_digit_display_2 (.value(n74163_2_pin14));  // open: dp
  Hex_Digit_Display hex_digit_display_3 (.value(n74163_3_pin15));  // open: dp
  _74163 #(.ShowInternalStructure("true")) u_74163_3 (
    .pin1(nRST), .pin2(clock_1_out), .pin3(n74163_1_pin3), .pin4(n74163_1_pin3), .pin5(n74163_1_pin3),
    .pin6(n74163_1_pin3), .pin7(n74163_2_pin15), .pin15(n74163_3_pin15[0]), .pin14(n74163_3_pin15[1]),
    .pin13(n74163_3_pin15[2]), .pin12(n74163_3_pin15[3]), .pin10(n74163_2_pin15), .pin9(n74163_1_pin7));  // open: pin11
  // also tied to GND on the sheet: n74163_1_pin3
  // also tied to VCC on the sheet: n74163_1_pin7
endmodule
